# Fritzing sketch Senseair_s8_lcd (saved by Fritzing 0.9.3b)
breadboards: 1

parts:
  TD-er1 = MH-Z19 CO2 sensor [part_number=MH-Z19]
  Part1 = Arduino Uno (Rev3)
  U1 = LCD-16X2 [package=lcd-8x2-kit]
  R1 = Resistor [tolerance=±5% resistance=220 package=THT]
  R2 = Rotary Potentiometer (Small) [maximum_resistance=100kΩ package=THT]

nets:
  N1: TD-er1.RX, Part1.A3
  N2: TD-er1.TX, Part1.A2
  VIN: TD-er1.Vin, Part1.5V, U1.VDD, R1.Pin_1, R2.leg1
  GND: TD-er1.GND, Part1.GND, U1.VSS, U1.R_W, U1.K, R2.leg2
  N3: Part1.D11_PWM/MOSI, U1.E
  N4: Part1.D12/MISO, U1.RS
  N5: Part1.D2, U1.DB7
  N6: Part1.D3_PWM, U1.DB6
  N7: Part1.D4, U1.DB5
  N8: Part1.D5_PWM, U1.DB4
  N9: U1.VO, R2.wiper
  N10: U1.A, R1.Pin_0
