# Fritzing sketch Senseair_s8_lcd (saved by Fritzing 1.0.1rc)
breadboards: 1

parts:
  TD-er1 = MH-Z19 CO2 sensor [part_number=MH-Z19]
  Part1 = Arduino Uno (Rev3)
  U1 = LCD-16X2 [package=lcd-8x2-kit]
  R1 = Resistor [tolerance=±5% resistance=220 power=0.25 package=THT]
  R2 = Rotary Potentiometer (Small) [maximum_resistance=100kΩ knob_status=50% package=THT]
  U2 = ESP8266 NodeMCU LoLin module
  Part2 = Logic Level Converter

nets:
  N1: TD-er1.RX, Part1.A3
  N2: TD-er1.TX, Part1.A2
  VIN: TD-er1.Vin, Part1.5V, U1.VDD, R1.Pin_1, R2.leg1, Part2.HV
  GND: TD-er1.GND, Part1.GND, U1.VSS, U1.R_W, U1.K, R2.leg2, U2.GND, Part2.GND
  N3: Part1.D11_PWM/MOSI, U1.E
  N4: Part1.D12/MISO, U1.RS
  N5: Part1.D0/RX, Part2.TX_HV
  N6: Part1.D1/TX, Part2.RX_HV
  N7: Part1.D2, U1.DB7
  N8: Part1.D3_PWM, U1.DB6
  N9: Part1.D4, U1.DB5
  N10: Part1.D5_PWM, U1.DB4
  N11: U1.VO, R2.wiper
  N12: U1.A, R1.Pin_0
  N13: U2.3V3, Part2.LV
  N14: U2.RX, Part2.RX_LV
  N15: U2.TX, Part2.TX_LV

custom parts:
  ESP8266 NodeMCU LoLin module: ESP8266 based NodeMCU
